# Fritzing sketch Forest Alert Firtzing  (saved by Fritzing 0.9.4)
breadboards: 1

parts:
  Argon1 = Particle Argon
  M1 = BMP280
  Grove1 = Grove Dust Sensor
  Q1 = PNP-Transistor [package="TO92 [THT]"]
  R1 = Resistor [tolerance=±5% resistance=220 package=THT]
  U1 = LIPO-1000mAh [package=lipo-1000]  # not connected
  D1 = SOLAR-IXYS [package=solarbit-12x1]
  M3 = fc-51 [package=THT]
  U2 = SUP500F [package=sup500f]
  F1 = Fan - Ventilador [package=THT]
  R2 = Resistor [tolerance=±5% resistance=220 package=THT]

nets:
  VCC: Argon1.3.3V, M1.VIN, Grove1.VCC, R1.Pin_0, M3.pin3, U2.VCC
  GND: Argon1.GND, M1.GND, Grove1.GND, Q1.B, D1.C, M3.pin2, U2.GND, F1.GND
  N1: Argon1.MI, U2.RX-I
  N2: Argon1.RX, U2.TX-O
  N3: Argon1.SDA, M1.SCL, Grove1.NC#1
  N4: Argon1.SCL, M1.SDA, Grove1.NC#5
  N5: Argon1.D3, R2.Pin_0
  N6: Argon1.D4, M3.pin1
  N7: Argon1.LI+, D1.A
  N8: Q1.E, R1.Pin_1, F1.5V
  N9: Q1.C, R2.Pin_1

custom parts:
  Particle Argon: The Argon is a powerful Wi-Fi enabled development board that can act as either a standalone Wi-Fi endpoint or Wi-Fi enabled gateway for Particle Mesh networks. It is based on the Nordic nRF52840 and has built-in battery charging circuitry so it’s easy to connect a Li-Po and deploy your local network in minutes. The Argon is great for connecting existing projects to the Particle Device Cloud or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
  BMP280: Temperature Humidity Barometric presure Sensor, I2C
  Grove Dust Sensor: PPD42 Grove Dust Sensor
  Fan - Ventilador: Ventilador de 2 pines, se encuentra comunmente en computadoras de escritorio
